# Fritzing sketch Untitled Sketch 2 (saved by Fritzing 0.9.3b)
breadboards: 1

parts:
  GY1 = MPU-6050 Board GY-521 [form="♀ (female)" package=THT]
  M1 = DC Motor  # not connected
  M2 = DC Motor  # not connected
  Part2 = Arduino Nano (Rev3.0)
  L298N1 = L298N DC motor driver
  VCC1 = Battery

nets:
  5V: GY1.pin1, Part2.5V, L298N1.5V
  N1: GY1.pin2, Part2.GND, VCC1.-
  N2: GY1.pin3, Part2.A5, Part2.A2
  N3: GY1.pin4, Part2.A4, Part2.A1
  N4: GY1.pin8, Part2.D2, Part2.D13/SCK
  N5: Part2.D1/TX, Part2.VIN, VCC1.+
  N6: Part2.D3, L298N1.ENA
  N7: Part2.D4, L298N1.IN1
  N8: Part2.D5, L298N1.IN2
  N9: Part2.D6, L298N1.IN3
  N10: Part2.D7, L298N1.ENB
  N11: Part2.D8, L298N1.IN4

custom parts:
  MPU-6050 Board GY-521: Acelerometro y Giroscopio MPU-6050 Board GY-521
  L298N DC motor driver: 2x DC motor driver with 78M05 positive voltage regulator (7..35 V) L298N: max 46 V, 2 A Set 5 V Enable jumper to enable 5 V regultor (needed for the L298N) and +5 V output at screw terminal or supply external +5 V at screw terminal Set ENA and/or ENB to +5 V to enable motor permanently or supply ENA and/or ENB with PWM signal IN1 and IN2 set rotation directory for motor A (OUT1/OUT2) IN2 and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
